# Fritzing sketch Greenhouse (saved by Fritzing 0.9.4)
breadboards: 1

parts:
  Part1 = Arduino Uno (Rev3) - ICSP
  KY-1 = Keyes Relay [package=THT]
  Part2 = LCD1602-I2C
  Part3 = Soil Moisture Sensor
  KY-2 = Keyes Relay [package=THT]
  WATER_PUMP1 = water pump/motor
  LED1 = LED - 5mm [color="Red (633nm)" package="5 mm [THT]"]
  S1 = Pushbutton [package="[THT]"]  # not connected
  J3 = Peltier Element
  LED2 = LED - 5mm [color="Blue (470nm)" package="5 mm [THT]"]
  LED3 = LED - 5mm [color="Yellow (595nm)" package="5 mm [THT]"]
  LED4 = LED - 5mm [color="Green (555nm)" package="5 mm [THT]"]
  KY-3 = Keyes Relay [package=THT]
  J5 = Power Jack [package=power_jack_slot]
  D2 = Diode [package=diode-1n4001]
  D3 = Diode [package=diode-1n4001]
  D4 = Diode [package=diode-1n4001]
  BULB1 = custom_light_bulb sm
  J6 = Power Jack [package=power_jack_slot]
  Mod1 = KY-015 Temperature & Humidity Sensor Module [package="Breakout board"]
  F2 = Fan - Ventilador [package=THT]
  F3 = Fan - Ventilador [package=THT]
  J7 = Peltier Element

nets:
  N1: Part1.A0, Part3.SIG
  N2: Part1.A1, Mod1.S
  N3: Part1.A4/SDA, Part2.SDA
  N4: Part1.A5/SCL, Part2.SCL
  VCC: Part1.5V, KY-1.power, Part2.VCC, Part3.VCC, KY-2.power, KY-3.power, Mod1.Vin
  N5: Part1.D8, LED2.anode
  N6: Part1.D9_PWM, LED1.anode
  N7: Part1.D3_PWM, KY-1.signal
  N8: Part1.D4, KY-2.signal
  N9: Part1.D5_PWM, KY-3.signal
  N10: Part1.D6_PWM, LED4.anode
  N11: Part1.D7, LED3.anode
  GND: Part1.GND, KY-1.ground, Part2.GND, Part3.GND, KY-2.ground, LED1.cathode, LED2.cathode, LED3.cathode, LED4.cathode, KY-3.ground, J5.GND, Mod1.-
  N12: Part1.VIN, J5.PWR
  N13: KY-1.C, KY-2.C, KY-3.C, J6.GND
  N14: KY-1.NO, WATER_PUMP1.pin_1
  N15: KY-2.NO, F3.GND, J7.pin2
  N16: WATER_PUMP1.pin_2, D3.C
  N17: J3.pin1, KY-3.NO, BULB1.connector1, F2.GND
  N18: J3.pin2, D4.C
  N19: D2.A, D3.A, D4.A, BULB1.connector0, J6.PWR
  5V: D2.C, F2.5V, F3.5V, J7.pin1

notes:
  12v Power Energy
  Water Pump / Motor
  Peltier Heater
  Fan Ventilador
  HEATER
  Bulb
  LCD I2c
  Temp
  Senor
  Relay
  Soil Moisture Sensor
  Fan Ventilador
  COOLER
  Peltier Cooler

custom parts:
  Keyes Relay: The Keyes 5V relay module is suitable for SCM development, home appliance control. It uses a 5V~12V TIL control signal which can control DC / AC signal.
  LCD1602-I2C: A standard character display, usually with 2x16 characters. Comes in many colors with LCM1602 IIC attached.
  water pump/motor: WATER PUMP BY ARDUBLOCKTR
  KY-015 Temperature & Humidity Sensor Module: KY-015 temperature and humidity sensor module, provides a low-latency serial interface to measure humidity and temperature.
  Fan - Ventilador: Ventilador de 2 pines, se encuentra comunmente en computadoras de escritorio
